// Logisim project Final_C2_Group_8.circ as structural Verilog: 12 circuits, main circuit Main_Ckt
module FPA_IC_ckt (
  input  [31:0] X,
  input  [31:0] Y,
  output Inf,
  output NaN,
  output Overflow,
  output Zero,
  output Denorm,
  output Underflow,
  output [31:0] fpa_Output,
  output [8:0] larger_exponent,
  output [8:0] exponent_diff,
  output mantissa_all_zero,
  output [4:0] shift_amount,
  output [27:0] normalized_mantissa,
  output [8:0] final_exponent,
  output [21:0] final_significand
);

  wire Adjust_InputX_inf, Adjust_InputX_nan, Adjust_InputY_inf, Adjust_InputY_nan, and_1_out,
       Custom_Comparator_exp_x_one, Custom_Comparator_exp_x_zero, Custom_Comparator_exp_y_one,
       Custom_Comparator_exp_y_zero, Custom_Comparator_xgey, FlagGenCkt_inf, FlagGenCkt_nan,
       Init_Inf_NaN_Check_inf, Init_Inf_NaN_Check_nan, Normalizer_is_denormal_zero,
       Rounding_Circuit_extra_shift_flag;
  wire [22:22] Rounding_Circuit_final_significand;
  wire [27:0] Adjust_InputX_adjusted_significand, Adjust_InputY_adjusted_significand,
       Significand_Adder_adjusted_significand;

  Comparator Custom_Comparator (
    .Exponent_X(X[30:22]), .Exponent_Y(Y[30:22]), .XgeY(Custom_Comparator_xgey), .difference(exponent_diff),
    .larger_exponent(larger_exponent), .exp_X_zero(Custom_Comparator_exp_x_zero),
    .exp_Y_zero(Custom_Comparator_exp_y_zero), .exp_X_one(Custom_Comparator_exp_x_one),
    .exp_Y_one(Custom_Comparator_exp_y_one));  // open: XltY
  and and_1 (and_1_out, Custom_Comparator_exp_y_zero, Custom_Comparator_exp_x_zero);
  Adjust_Exponent_e9a03ee2 Adjust_Exponent (
    .Extra_Shift(Rounding_Circuit_extra_shift_flag), .Larger_Exponent(larger_exponent),
    .Shift_Amount(shift_amount), .is_result_zero(mantissa_all_zero), .Final_Exponent(final_exponent),
    .Exponent_Overflow(Overflow), .Exponent_Neg(Underflow));
  Adjust_Input_35949ddf Adjust_InputX (
    .mantissa(X[21:0]), .exp_zero(Custom_Comparator_exp_x_zero), .sign_bit(X[31]),
    .exp_one(Custom_Comparator_exp_x_one), .Adjusted_Significand(Adjust_InputX_adjusted_significand),
    .Inf(Adjust_InputX_inf), .NaN(Adjust_InputX_nan));
  Adjust_Input_35949ddf Adjust_InputY (
    .mantissa(Y[21:0]), .exp_zero(Custom_Comparator_exp_y_zero), .sign_bit(Y[31]),
    .exp_one(Custom_Comparator_exp_y_one), .Adjusted_Significand(Adjust_InputY_adjusted_significand),
    .Inf(Adjust_InputY_inf), .NaN(Adjust_InputY_nan));
  Significand_Adder_4ebd4a6a Significand_Adder (
    .Significand_X(Adjust_InputX_adjusted_significand), .Significand_Y(Adjust_InputY_adjusted_significand),
    .XgeY(Custom_Comparator_xgey), .Shifiting_Amount(exponent_diff),
    .Adjusted_Significand(Significand_Adder_adjusted_significand), .Sign_bit(fpa_Output[31]));
  Normailzation Normalizer (
    .Non_normalized_Significand(Significand_Adder_adjusted_significand), .both_exp_zero(and_1_out),
    .Normalized_Significand(normalized_mantissa), .Shift_Amount(shift_amount),
    .Mantissa_Zero(mantissa_all_zero), .is_denormal_zero(Normalizer_is_denormal_zero));
  Rounding_Circuit_d28f778d Rounding_Circuit (
    .Normalized_Significand(normalized_mantissa), .is_denormal(Normalizer_is_denormal_zero),
    .Final_Significand({Rounding_Circuit_final_significand[22], final_significand}),
    .Extra_Shift_Flag(Rounding_Circuit_extra_shift_flag));
  Init_Inf_NaN_Checker Init_Inf_NaN_Check (
    .X_inf(Adjust_InputY_inf), .Y_inf(Adjust_InputX_inf), .X_NaN(Adjust_InputY_nan),
    .Y_NaN(Adjust_InputX_nan), .Inf(Init_Inf_NaN_Check_inf), .NaN(Init_Inf_NaN_Check_nan));
  Flags_gen_ckt FlagGenCkt (
    .input_final_mantissa(final_significand), .significand_bit(Rounding_Circuit_final_significand[22]),
    .final_exponent(final_exponent), .Inf(FlagGenCkt_inf), .Zero(Zero), .NaN(FlagGenCkt_nan),
    .Denormalized(Denorm));
  or or_1 (Inf, Init_Inf_NaN_Check_inf, FlagGenCkt_inf);
  or or_2 (NaN, Init_Inf_NaN_Check_nan, FlagGenCkt_nan);

  assign fpa_Output[30:0] = {final_exponent, final_significand};
endmodule

module Adjust_Input_35949ddf (
  input  [21:0] mantissa,
  input  exp_zero,
  input  sign_bit,
  input  exp_one,
  output [27:0] Adjusted_Significand,
  output Inf,
  output NaN
);

  wire nor_1_out, not_2_out;
  wire [25:25] not_1_out;
  wire [27:0] negator_1_out;

  not not_1 (not_1_out[25], exp_zero);
  nor nor_1 (nor_1_out, mantissa[21], mantissa[20], mantissa[19], mantissa[18], mantissa[17], mantissa[16], mantissa[15], mantissa[14], mantissa[13], mantissa[12], mantissa[11], mantissa[10], mantissa[9], mantissa[8], mantissa[7], mantissa[6], mantissa[5], mantissa[4], mantissa[3], mantissa[2], mantissa[1], mantissa[0]);
  Negator #(.width(28)) negator_1 (.in({2'b00, not_1_out[25], mantissa, 3'b000}), .out(negator_1_out));
  not not_2 (not_2_out, nor_1_out);
  and and_1 (Inf, nor_1_out, exp_one);
  and and_2 (NaN, not_2_out, exp_one);
  Multiplexer #(.width(28)) multiplexer_1 (
    .in0({2'b00, not_1_out[25], mantissa, 3'b000}), .in1(negator_1_out), .out(Adjusted_Significand),
    .sel(sign_bit));
endmodule

module Comparator (
  input  [8:0] Exponent_X,
  input  [8:0] Exponent_Y,
  output XgeY,
  output XltY,
  output [8:0] difference,
  output [8:0] larger_exponent,
  output exp_X_zero,
  output exp_Y_zero,
  output exp_X_one,
  output exp_Y_one
);

  wire comparator_1_eq, comparator_1_gt, or_2_out;
  wire [8:0] multiplexer_1_out, subtractor_1_out;

  Comparator_part #(.mode("unsigned"), .width(9)) comparator_1 (
    .a(Exponent_X), .b(Exponent_Y), .gt(comparator_1_gt), .eq(comparator_1_eq), .lt(XltY));
  or or_1 (XgeY, comparator_1_gt, comparator_1_eq);
  Multiplexer #(.width(9)) multiplexer_1 (.in0(Exponent_X), .in1(Exponent_Y), .out(multiplexer_1_out), .sel(XgeY));
  Multiplexer #(.width(9)) multiplexer_2 (.in0(Exponent_X), .in1(Exponent_Y), .out(larger_exponent), .sel(XltY));
  nor nor_1 (exp_X_zero, Exponent_X[0], Exponent_X[1], Exponent_X[2], Exponent_X[3], Exponent_X[4], Exponent_X[5], Exponent_X[6], Exponent_X[7], Exponent_X[8]);
  nor nor_2 (exp_Y_zero, Exponent_Y[0], Exponent_Y[1], Exponent_Y[2], Exponent_Y[3], Exponent_Y[4], Exponent_Y[5], Exponent_Y[6], Exponent_Y[7], Exponent_Y[8]);
  and and_1 (exp_X_one, Exponent_X[0], Exponent_X[1], Exponent_X[2], Exponent_X[3], Exponent_X[4], Exponent_X[5], Exponent_X[6], Exponent_X[7], Exponent_X[8]);
  and and_2 (exp_Y_one, Exponent_Y[0], Exponent_Y[1], Exponent_Y[2], Exponent_Y[3], Exponent_Y[4], Exponent_Y[5], Exponent_Y[6], Exponent_Y[7], Exponent_Y[8]);
  Subtractor #(.width(9)) subtractor_1 (
    .a(larger_exponent), .b(multiplexer_1_out), .out(subtractor_1_out), .bin(1'b0));  // open: bout
  Multiplexer #(.width(9)) multiplexer_3 (.in0(subtractor_1_out), .in1({9{1'b0}}), .out(difference), .sel(or_2_out));
  or or_2 (or_2_out, exp_X_zero, exp_Y_zero);

  // Notes on the sheet:
  //   X>=Y
  //   Denormal/Zero Number Handling
  //   Inf/NaN Number Handling
  //   smaller
  //   larger
endmodule

module Significand_Adder_4ebd4a6a (
  input  [27:0] Significand_X,
  input  [27:0] Significand_Y,
  input  XgeY,
  input  [8:0] Shifiting_Amount,
  output [27:0] Adjusted_Significand,
  output Sign_bit
);

  wire not_2_out, or_1_out;
  wire [26:0] adder_2_out;
  wire [27:0] adder_1_out, multiplexer_1_out, multiplexer_3_out, multiplexer_4_out, not_1_out, shifter_1_out;

  assign not_1_out = ~{Sign_bit, adder_2_out};  // NOT_Gate not_1, 28 bits wide
  Adder #(.width(28)) adder_1 (.a(not_1_out), .b(28'h1), .out(adder_1_out), .cin(1'b0));  // open: cout
  Multiplexer #(.width(28)) multiplexer_1 (
    .in0(Significand_X), .in1(Significand_Y), .out(multiplexer_1_out), .sel(XgeY));
  not not_2 (not_2_out, XgeY);
  Shifter #(.shift("ar"), .width(28)) shifter_1 (
    .in(multiplexer_1_out), .\dist (Shifiting_Amount[4:0]), .out(shifter_1_out));
  Multiplexer #(.width(28)) multiplexer_2 (
    .in0({Sign_bit, adder_2_out}), .in1(adder_1_out), .out(Adjusted_Significand), .sel(Sign_bit));
  Multiplexer #(.width(28)) multiplexer_3 (
    .in0(Significand_X), .in1(Significand_Y), .out(multiplexer_3_out), .sel(not_2_out));
  Multiplexer #(.width(28)) multiplexer_4 (
    .in0(shifter_1_out), .in1({28{1'b0}}), .out(multiplexer_4_out), .sel(or_1_out));
  or or_1 (or_1_out, Shifiting_Amount[5], Shifiting_Amount[6], Shifiting_Amount[7], Shifiting_Amount[8]);
  Adder #(.width(28)) adder_2 (
    .a(multiplexer_3_out), .b(multiplexer_4_out), .out({Sign_bit, adder_2_out}), .cin(1'b0));  // open: cout

  // Notes on the sheet:
  //   Smaller
  //   Larger
endmodule

module Adjusting_sign_bit_1a93fe9b (
  input  [25:0] Initial_Significand_21ba6ef2,
  output [25:0] Adjusted_Significand_4e98976d,
  output Sign_bit_9e5a82a6
);

  wire [25:0] adder_1_out, not_1_out;

  assign not_1_out = ~Initial_Significand_21ba6ef2;  // NOT_Gate not_1, 26 bits wide
  Adder #(.width(26)) adder_1 (.a(not_1_out), .b(26'h1), .out(adder_1_out), .cin(1'b0));  // open: cout
  Multiplexer #(.width(26)) multiplexer_1 (
    .in0(Initial_Significand_21ba6ef2), .in1(adder_1_out), .out(Adjusted_Significand_4e98976d),
    .sel(Initial_Significand_21ba6ef2[25]));

  assign Sign_bit_9e5a82a6 = Initial_Significand_21ba6ef2[25];
endmodule

module Normailzation (
  input  [27:0] Non_normalized_Significand,
  input  both_exp_zero,
  output [27:0] Normalized_Significand,
  output [4:0] Shift_Amount,
  output Mantissa_Zero,
  output is_denormal_zero
);

  wire and_2_out, not_1_out, priority_encoder_1_gs;
  wire [4:0] multiplexer_1_out, priority_encoder_1_out, subtractor_1_out;
  wire [31:0] bit_extender_1_out;

  assign bit_extender_1_out = {{4{Non_normalized_Significand[27]}}, Non_normalized_Significand};  // Bit_Extender bit_extender_1
  not not_1 (not_1_out, Non_normalized_Significand[25]);
  Priority_Encoder #(.select(5)) priority_encoder_1 (
    .in0(bit_extender_1_out[0]), .in1(bit_extender_1_out[1]), .in2(bit_extender_1_out[2]),
    .in3(bit_extender_1_out[3]), .in4(bit_extender_1_out[4]), .in5(bit_extender_1_out[5]),
    .in6(bit_extender_1_out[6]), .in7(bit_extender_1_out[7]), .in8(bit_extender_1_out[8]),
    .in9(bit_extender_1_out[9]), .in10(bit_extender_1_out[10]), .in11(bit_extender_1_out[11]),
    .in12(bit_extender_1_out[12]), .in13(bit_extender_1_out[13]), .in14(bit_extender_1_out[14]),
    .in15(bit_extender_1_out[15]), .in16(bit_extender_1_out[16]), .in17(bit_extender_1_out[17]),
    .in18(bit_extender_1_out[18]), .in19(bit_extender_1_out[19]), .in20(bit_extender_1_out[20]),
    .in21(bit_extender_1_out[21]), .in22(bit_extender_1_out[22]), .in23(bit_extender_1_out[23]),
    .in24(bit_extender_1_out[24]), .in25(bit_extender_1_out[25]), .in26(bit_extender_1_out[26]),
    .in27(bit_extender_1_out[27]), .in28(bit_extender_1_out[28]), .in29(bit_extender_1_out[29]),
    .in30(bit_extender_1_out[30]), .in31(bit_extender_1_out[31]), .out(priority_encoder_1_out),
    .gs(priority_encoder_1_gs), .en_in(1'b1));  // open: en_out
  not not_2 (Mantissa_Zero, priority_encoder_1_gs);
  and and_1 (is_denormal_zero, both_exp_zero, not_1_out);
  Multiplexer #(.select(2), .width(5)) multiplexer_1 (
    .in0(priority_encoder_1_out), .in1(5'b11001), .in2(5'b11001), .in3(5'b11001), .out(multiplexer_1_out),
    .sel({is_denormal_zero, Mantissa_Zero}));
  Subtractor #(.width(5)) subtractor_1 (
    .a(5'b11011), .b(multiplexer_1_out), .out(subtractor_1_out), .bin(1'b0));  // open: bout
  and and_2 (and_2_out, both_exp_zero, Non_normalized_Significand[25]);
  Shifter #(.width(28)) shifter_1 (
    .in(Non_normalized_Significand), .\dist (subtractor_1_out), .out(Normalized_Significand));
  Multiplexer #(.width(5)) multiplexer_2 (.in0(subtractor_1_out), .in1(5'b00001), .out(Shift_Amount), .sel(and_2_out));

  // Notes on the sheet:
  //   Case Handling
  //   Note
  //    Otherwise it will look like any other normal number
  //   Denormal + Denormal → Denormal or zero or Normal (if result is large enough)
  //   if we remember the case where we have to right shift once in case of overflow on implicit significand.
  //    In this case, denormals do not have any implicit 1, so when we get normal number by adding two denormal, extra exponent has to be added.
  //   when denormal + denormal = normal, the shift amount is 2-1 = 1
  //   2 is always needed to omit first two extra bit. 
  //    It will be subtracted from exponent later
  //   After that, to add 1 to exponent we subtracted 1from shift amount as
endmodule

module Rounding_Circuit_d28f778d (
  input  [27:0] Normalized_Significand,
  input  is_denormal,
  output [22:0] Final_Significand,
  output Extra_Shift_Flag
);

  wire and_1_out, and_2_out, and_3_out, not_1_out, not_2_out, or_1_out, or_2_out;
  wire [22:0] adder_1_out, bit_extender_1_out, shifter_1_out;

  not not_1 (not_1_out, is_denormal);
  or or_1 (or_1_out, Normalized_Significand[0], Normalized_Significand[1], Normalized_Significand[2]);
  not not_2 (not_2_out, Normalized_Significand[3]);
  and and_1 (and_1_out, or_1_out, not_2_out);
  or or_2 (or_2_out, and_1_out, Normalized_Significand[3], Normalized_Significand[5]);
  and and_2 (and_2_out, or_2_out, Normalized_Significand[4]);
  and and_3 (and_3_out, and_2_out, not_1_out);
  assign bit_extender_1_out = {{22{1'b0}}, and_3_out};  // Bit_Extender bit_extender_1
  Adder #(.width(23)) adder_1 (
    .a(bit_extender_1_out), .b(Normalized_Significand[27:5]), .out(adder_1_out), .cin(1'b0),
    .cout(Extra_Shift_Flag));
  Shifter #(.shift("lr"), .width(23)) shifter_1 (.in(adder_1_out), .\dist (5'b00001), .out(shifter_1_out));
  Multiplexer #(.width(23)) multiplexer_1 (
    .in0(adder_1_out), .in1({1'b1, shifter_1_out[21:0]}), .out(Final_Significand), .sel(Extra_Shift_Flag));

  // Notes on the sheet:
  //   rounding not needed for denormal result
  //   round = G(L+SR'+R)
  //   L | G | R | S | round
  //   0 | 1 | 0 | 0 | 0
  //   1 | 1 | 0 | 0 | 1
  //   X | 1 | 0 | 1 | 1
  //   X | 1 | 1 | X | 1
  //   Here extra right shift is needed for the case when rouding overflows
endmodule

module Adjust_Exponent_e9a03ee2 (
  input  Extra_Shift,
  input  [8:0] Larger_Exponent,
  input  [4:0] Shift_Amount,
  input  is_result_zero,
  output [8:0] Final_Exponent,
  output Exponent_Overflow,
  output Exponent_Neg
);

  wire not_1_out;
  wire [9:0] adder_1_out, subtractor_1_out;

  Adder #(.width(10)) adder_1 (
    .a({1'b0, Larger_Exponent}), .b(10'h2), .out(adder_1_out), .cin(Extra_Shift));  // open: cout
  Subtractor #(.width(10)) subtractor_1 (
    .a(adder_1_out), .b({{5{1'b0}}, Shift_Amount}), .out(subtractor_1_out), .bin(1'b0), .bout(Exponent_Neg));
  not not_1 (not_1_out, Exponent_Neg);
  Multiplexer #(.select(3), .width(9)) multiplexer_1 (
    .in0(subtractor_1_out[8:0]), .in1({9{1'b0}}), .in2({9{1'b1}}), .in3({9{1'b0}}), .in4({9{1'b0}}),
    .in5({9{1'b0}}), .in6({9{1'b0}}), .in7({9{1'b0}}), .out(Final_Exponent),
    .sel({is_result_zero, Exponent_Overflow, Exponent_Neg}));
  and and_1 (Exponent_Overflow, subtractor_1_out[9], not_1_out);

  // Notes on the sheet:
  //   But the newly added bit could be 1 for two cases :
  //   -overflow happens while adding
  //   We added extra bit in front of exponent to detect overflow while adding (+2 at max). 
  //   So if the exponent is 11...11 or 11...10, there is chance that we go out of bound for the exponent
  //   - underflow happens while subtracting. If A<B, then A-B always yields the first bit as 1
  //   We can overcome this case by looking at borrow out of the subtractor. B(out) is 1 when A<B
  //   Z | O | N | E
  //   -------------------
  //   0 | 0 | 0 | result
  //   0 | X | 1 | 0
  //   0 | 1 | 0 | 511
  //   1 | X | X | 0
endmodule

module Main_Ckt (
  input  [31:0] Input_X,
  input  [31:0] Input_Y,
  output Inf,
  output NaN,
  output Overflow_Flag,
  output Zero,
  output Denormalized,
  output Underflow_Flag,
  output [31:0] Output_Z
);

  FPA_IC_ckt FPA_IC (
    .Inf(Inf), .NaN(NaN), .Overflow(Overflow_Flag), .Zero(Zero), .Denorm(Denormalized),
    .Underflow(Underflow_Flag), .fpa_Output(Output_Z), .X(Input_X), .Y(Input_Y));  // open: larger_exponent, mantissa_all_zero, shift_amount, exponent_diff, normalized_mantissa, final_exponent, final_significand
endmodule

module zero_checker (
  input  Implicit_significand,
  input  Mantissa_zero,
  output is_result_zero
);

  wire not_1_out;

  not not_1 (not_1_out, Implicit_significand);
  and and_1 (is_result_zero, not_1_out, Mantissa_zero);
endmodule

module Flags_gen_ckt (
  input  [21:0] input_final_mantissa,
  input  significand_bit,
  input  [8:0] final_exponent,
  output Inf,
  output Zero,
  output NaN,
  output Denormalized
);

  wire and_1_out, nor_1_out, nor_2_out, not_1_out, not_2_out, or_1_out;

  and and_1 (and_1_out, final_exponent[0], final_exponent[1], final_exponent[2], final_exponent[3], final_exponent[4], final_exponent[5], final_exponent[6], final_exponent[7], final_exponent[8]);
  nor nor_1 (nor_1_out, final_exponent[8], final_exponent[7], final_exponent[6], final_exponent[5], final_exponent[4], final_exponent[3], final_exponent[2], final_exponent[1], final_exponent[0]);
  nor nor_2 (nor_2_out, input_final_mantissa[0], input_final_mantissa[1], input_final_mantissa[2], input_final_mantissa[3], input_final_mantissa[4], input_final_mantissa[5], input_final_mantissa[6], input_final_mantissa[7], input_final_mantissa[8], input_final_mantissa[9], input_final_mantissa[10], input_final_mantissa[11], input_final_mantissa[12], input_final_mantissa[13], input_final_mantissa[14], input_final_mantissa[15], input_final_mantissa[16], input_final_mantissa[17], input_final_mantissa[18], input_final_mantissa[19], input_final_mantissa[20], input_final_mantissa[21]);
  not not_1 (not_1_out, nor_2_out);
  not not_2 (not_2_out, significand_bit);
  or or_1 (or_1_out, not_1_out, significand_bit);
  and and_2 (Inf, nor_2_out, and_1_out);
  and and_3 (Zero, nor_2_out, not_2_out, nor_1_out);
  and and_4 (NaN, and_1_out, not_1_out);
  and and_5 (Denormalized, or_1_out, nor_1_out);

  // Notes on the sheet:
  //   Interesting Case: 1.1 * 2e(-254) + 1.0 *2e(-254) = 1.00 * 2e(-255)
  //   all zero
  //   at least one 1 bit
endmodule

module Init_Inf_NaN_Checker (
  input  X_inf,
  input  Y_inf,
  input  X_NaN,
  input  Y_NaN,
  output Inf,
  output NaN
);

  wire nor_1_out, or_1_out;

  or or_1 (or_1_out, X_inf, Y_inf);
  nor nor_1 (nor_1_out, X_NaN, Y_NaN);
  not not_1 (NaN, nor_1_out);
  and and_1 (Inf, or_1_out, nor_1_out);

  // Notes on the sheet:
  //   If one of the input is NaN,
  //    then the NaN will get priority
endmodule
