// Logisim project MIPS(backup).circ as structural Verilog: 4 circuits, main circuit main
module main (
  input  CLR,
  output [7:0] PC_2__relative_to_ID_instruction,
  output [1:0] out_3,
  output [7:0] PC_1_offset__relative_to_ID_instruction,
  output [1:0] out_5,
  output [7:0] Next_PC,
  output [7:0] out_7,
  output [7:0] zero,
  output [3:0] out_9,
  output [3:0] out_10,
  output [3:0] out_11,
  output [7:0] out_12,
  output [7:0] t0,
  output [7:0] out_14,
  output [7:0] out_15,
  output [19:0] out_16,
  output [7:0] t1,
  output [7:0] out_18,
  output [7:0] t2,
  output [7:0] t3,
  output [3:0] out_21,
  output [3:0] out_22,
  output [1:0] out_23,
  output [1:0] out_24,
  output [7:0] out_25,
  output [3:0] out_26,
  output [7:0] t4,
  output [7:0] out_28,
  output [7:0] out_29,
  output [7:0] sp,
  output [2:0] ALUControl,
  output [7:0] out_32
);

  wire and_1_out, and_2_out, CLK_out, comparator_1_eq, not_1_out, not_2_out, not_3_out, or_1_out, or_2_out,
       or_3_out;
  wire [1:0] ex_mem_1_out_8, ex_mem_1_out_9, id_ex_1_out_13, id_ex_1_out_14, loadhazardunit_1_flushstall,
       mem_wb_1_out_7;
  wire [3:0] id_ex_1_out_18, id_ex_1_out_19, id_ex_1_out_20;
  wire [5:3] id_ex_1_out_15;
  wire [7:0] bit_extender_1_out, ex_mem_1_out_10, ex_mem_1_out_11, id_ex_1_out_16, id_ex_1_out_17,
       id_ex_1_out_21, main_1_read_data_1, mem_wb_1_out_8, mem_wb_1_out_9, multiplexer_2_out,
       multiplexer_7_out, multiplexer_8_out, multiplexer_10_out, multiplexer_11_out, multiplexer_12_out,
       PC_q, ram_1_data, subtractor_1_out;
  wire [12:0] multiplexer_5_out, rom_2_data;
  wire [19:0] multiplexer_4_out, rom_1_data;

  Clock CLK (.out(CLK_out));
  Multiplexer #(.width(8), .enable("false")) multiplexer_1 (
    .in0(multiplexer_2_out), .in1({out_10, out_11}), .out(Next_PC), .sel(multiplexer_5_out[12]));
  Register PC (.D(Next_PC), .en(1'b1), .Q(PC_q), .clk(CLK_out), .clr(CLR));
  Subtractor subtractor_1 (.a(PC_q), .b(8'h2), .out(subtractor_1_out));  // open: bin, bout
  Multiplexer #(.width(8), .enable("false")) multiplexer_2 (
    .in0(out_28), .in1(PC_1_offset__relative_to_ID_instruction), .out(multiplexer_2_out), .sel(or_3_out));
  Multiplexer #(.width(8), .enable("false")) multiplexer_3 (
    .in0(PC_q), .in1(subtractor_1_out), .out(out_12), .sel(loadhazardunit_1_flushstall[1]));
  Adder adder_1 (.a(8'h1), .b(out_12), .out(out_28));  // open: cin, cout
  ROM #(.dataWidth(20)) rom_1 (.addr(out_12), .data(rom_1_data));  // open: sel
  or or_1 (or_1_out, multiplexer_5_out[12], or_3_out, loadhazardunit_1_flushstall[1]);
  Multiplexer #(.width(20), .enable("false")) multiplexer_4 (
    .in0(rom_1_data), .in1(20'h50000), .out(multiplexer_4_out), .sel(or_1_out));
  IF_ID if_id_1 (
    .PC(out_28), .Instruction(multiplexer_4_out), .CLK(CLK_out), .CLR(CLR), .PCEnable(1'b1), .PC_2(out_15),
    .Instruction_2({out_16[19:16], out_10, out_11, out_16[7:0]}));
  Adder adder_2 (.a(out_15), .b(out_16[7:0]), .out(PC_1_offset__relative_to_ID_instruction));  // open: cin, cout
  assign bit_extender_1_out = {{4{1'b0}}, out_16[3:0]};  // Bit_Extender bit_extender_1
  ROM #(.addrWidth(4), .dataWidth(13)) rom_2 (.addr(out_16[19:16]), .data(rom_2_data));  // open: sel
  LoadHazardUnit loadhazardunit_1 (
    .Instruction({out_16[19:16], out_10, out_11, out_16[7:0]}), .ID_EX_MemRead(id_ex_1_out_14[1]),
    .IF_ID_RegisterRs(out_10), .IF_ID_RegisterRt(out_11), .ID_EX_RegisterRt(out_21), .branch(or_2_out),
    .EX_MEM_MemRead(ex_mem_1_out_9[1]), .ID_EX_RegisterRs(id_ex_1_out_18), .EX_MEM_RegisterRd(out_26),
    .ID_EX_RegisterRt_2(id_ex_1_out_19), .flushstall(loadhazardunit_1_flushstall));
  not not_1 (not_1_out, CLK_out);
  or or_2 (or_2_out, rom_2_data[4], rom_2_data[5]);
  Multiplexer #(.width(13), .enable("false")) multiplexer_5 (
    .in0(rom_2_data), .in1({13{1'b0}}), .out(multiplexer_5_out), .sel(loadhazardunit_1_flushstall[0]));
  or or_3 (or_3_out, and_2_out, and_1_out);
  and and_1 (and_1_out, comparator_1_eq, multiplexer_5_out[5]);
  and and_2 (and_2_out, multiplexer_5_out[4], not_2_out);
  not not_2 (not_2_out, comparator_1_eq);
  Register_main main_1 (
    .Read_Register_1(out_10), .Read_Register_2(out_11), .Write_Register(out_9), .in_4(out_7),
    .Write_Signal(mem_wb_1_out_7[1]), .CLK(not_1_out), .Clear(CLR), .zero(zero), .t0(t0), .t1(t1), .t2(t2),
    .t3(t3), .t4(t4), .sp(sp), .Read_Data_1(main_1_read_data_1), .Read_Data_2(out_18));
  ID_EX id_ex_1 (
    .WB({multiplexer_5_out[9], multiplexer_5_out[6]}), .MEM(multiplexer_5_out[8:7]),
    .EX({multiplexer_5_out[11:10], multiplexer_5_out[3:0]}), .rs_data(main_1_read_data_1), .rt_data(out_18),
    .rs_address(out_10), .rt_address(out_11), .rd_address(out_16[7:4]), .shift_amount(bit_extender_1_out),
    .immediate_addr(out_16[7:0]), .CLR(CLR), .CLK(CLK_out), .out_13(id_ex_1_out_13), .out_14(id_ex_1_out_14),
    .out_15({id_ex_1_out_15, ALUControl}), .out_16(id_ex_1_out_16), .out_17(id_ex_1_out_17),
    .out_18(id_ex_1_out_18), .out_19(id_ex_1_out_19), .out_20(id_ex_1_out_20), .out_21(id_ex_1_out_21),
    .out_22(out_32));
  Multiplexer #(.width(4), .enable("false")) multiplexer_6 (
    .in0(id_ex_1_out_19), .in1(id_ex_1_out_20), .out(out_21), .sel(id_ex_1_out_15[4]));
  Multiplexer #(.select(2), .width(8), .enable("false")) multiplexer_7 (
    .in0(main_1_read_data_1), .in1(out_7), .in2(ex_mem_1_out_10), .out(multiplexer_7_out), .sel(out_3));  // open: in3
  Multiplexer #(.select(2), .width(8), .enable("false")) multiplexer_8 (
    .in0(out_18), .in1(out_7), .in2(ex_mem_1_out_10), .out(multiplexer_8_out), .sel(out_5));  // open: in3
  ForwardingUnit branchINsForward (
    .EX_MEM_RegWrite(ex_mem_1_out_8[1]), .EX_MEM_RegisterRd(out_26), .ID_EX_RegisterRs(out_10),
    .ID_EX_RegisterRt(out_11), .MEM_WB_RegWrite(mem_wb_1_out_7[0]), .MEM_WB_RegisterRd(out_9),
    .ForwardA(out_3), .out_8(out_5));
  Multiplexer #(.select(2), .width(8), .enable("false")) multiplexer_9 (
    .in0(id_ex_1_out_16), .in1(out_7), .in2(ex_mem_1_out_10), .out(out_29), .sel(out_23));  // open: in3
  Multiplexer #(.select(2), .width(8), .enable("false")) multiplexer_10 (
    .in0(id_ex_1_out_17), .in1(out_7), .in2(ex_mem_1_out_10), .out(multiplexer_10_out), .sel(out_24));  // open: in3
  ForwardingUnit forwardingunit_1 (
    .EX_MEM_RegWrite(ex_mem_1_out_8[1]), .EX_MEM_RegisterRd(out_26), .ID_EX_RegisterRs(id_ex_1_out_18),
    .ID_EX_RegisterRt(id_ex_1_out_19), .MEM_WB_RegWrite(mem_wb_1_out_7[1]), .MEM_WB_RegisterRd(out_9),
    .ForwardA(out_23), .out_8(out_24));
  Comparator comparator_1 (.a(multiplexer_7_out), .b(multiplexer_8_out), .eq(comparator_1_eq));  // open: gt, lt
  Multiplexer #(.width(8), .enable("false")) multiplexer_11 (
    .in0(out_29), .in1(id_ex_1_out_21), .out(multiplexer_11_out), .sel(id_ex_1_out_15[5]));
  Multiplexer #(.width(8), .enable("false")) multiplexer_12 (
    .in0(multiplexer_10_out), .in1(out_32), .out(multiplexer_12_out), .sel(id_ex_1_out_15[3]));
  // ALU_8_by_ART alu_8_by_art_1: pin names not known; wires that end beside it: id_ex_1_out_15[3], multiplexer_11_out, multiplexer_12_out, ALUControl, out_25
  EX_MEM ex_mem_1 (
    .WB(id_ex_1_out_13), .MEM(id_ex_1_out_14), .ALUoutput(out_25), .WriteData(multiplexer_10_out),
    .rd_address(out_21), .CLR(CLR), .CLK(CLK_out), .out_8(ex_mem_1_out_8), .out_9(ex_mem_1_out_9),
    .out_10(ex_mem_1_out_10), .out_11(ex_mem_1_out_11), .out_12(out_26));
  RAM #(.bus("separate")) ram_1 (
    .addr(ex_mem_1_out_10), .din(ex_mem_1_out_11), .data(ram_1_data), .str(ex_mem_1_out_9[0]),
    .clk(not_3_out), .ld(ex_mem_1_out_9[1]), .clr(CLR));  // open: sel
  not not_3 (not_3_out, CLK_out);
  MEM_WB mem_wb_1 (
    .WB(ex_mem_1_out_8), .DM_read_data(ram_1_data), .ALUoutput(ex_mem_1_out_10), .rd_address(out_26),
    .CLR(CLR), .CLK(CLK_out), .out_7(mem_wb_1_out_7), .out_8(mem_wb_1_out_8), .out_9(mem_wb_1_out_9),
    .out_10(out_9));
  Multiplexer #(.width(8), .enable("false")) multiplexer_13 (
    .in0(mem_wb_1_out_9), .in1(mem_wb_1_out_8), .out(out_7), .sel(mem_wb_1_out_7[0]));

  assign out_14 = out_7;
  assign out_16[15:8] = {out_10, out_11};
  assign out_22 = out_9;
  assign PC_2__relative_to_ID_instruction = out_28;

  // Notes on the sheet:
  //   Instruction Memory
  //   Caution: Clear once before running any instruction
  //   contents of rom_1 (hex, n*v repeats v):
  //   5010a 50201 e210b 50202 e2109 50201 50301 50502 d2340 d0320 d0430 55501 215fb a0f00 50401 16400 6601
  //   80414 16100 6601 b0155 16500 6601 155a2 16500 6601 c52a2 16200 6601 52388 16300 6601 3481 f4340
  //   16400 6601 50146 50255 91230 16300 6601 334fe 16400 6601 50480 505aa 64520 16200 6601 723ff 16300
  //   6601 a3400
  //   if hazard happens automatically freezes the PC and taken back to the branch instruction address with subtractor for NOP instruction,as another instruction is loaded after the branch instruction
  //   avoid instruction after branch if branch is taken
  //   Control Word Memory
  //   contents of rom_2 (hex, n*v repeats v):
  //   209 88 11 20b 604 208 602 20a e06 603 1000 e05 348 600 21 601
  //   Register
  //   Control Word Structure:
  //   jump | shift | RegDst | RegWrite | MemRead | MemWrite | MtoR | beq | bneq | ALUSrc | ALUControl
  //   ALU
  //   Data Memory
endmodule

module test (
  input  [3:0] in_1,
  input  [3:0] in_2,
  input  [3:0] in_3,
  input  [7:0] in_4,
  output [7:0] out_5,
  output [7:0] out_6
);

  wire clock_1_out;

  Clock clock_1 (.out(clock_1_out));
endmodule

module ForwardingUnit (
  input  EX_MEM_RegWrite,
  input  [3:0] EX_MEM_RegisterRd,
  input  [3:0] ID_EX_RegisterRs,
  input  [3:0] ID_EX_RegisterRt,
  input  MEM_WB_RegWrite,
  input  [3:0] MEM_WB_RegisterRd,
  output [1:0] ForwardA,
  output [1:0] out_8
);

  wire and_1_out, and_2_out, comparator_1_eq, comparator_2_eq, comparator_3_eq, comparator_4_eq,
       comparator_5_eq, comparator_6_eq, not_1_out, not_2_out, not_3_out, not_4_out;

  Comparator #(.width(4)) comparator_1 (.a(EX_MEM_RegisterRd), .b(4'b0000), .eq(comparator_1_eq));  // open: gt, lt
  Comparator #(.width(4)) comparator_2 (
    .a(EX_MEM_RegisterRd), .b(ID_EX_RegisterRs), .eq(comparator_2_eq));  // open: gt, lt
  Comparator #(.width(4)) comparator_3 (
    .a(EX_MEM_RegisterRd), .b(ID_EX_RegisterRt), .eq(comparator_3_eq));  // open: gt, lt
  Comparator #(.width(4)) comparator_4 (.a(MEM_WB_RegisterRd), .b(4'b0000), .eq(comparator_4_eq));  // open: gt, lt
  Comparator #(.width(4)) comparator_5 (
    .a(MEM_WB_RegisterRd), .b(ID_EX_RegisterRs), .eq(comparator_5_eq));  // open: gt, lt
  Comparator #(.width(4)) comparator_6 (
    .a(MEM_WB_RegisterRd), .b(ID_EX_RegisterRt), .eq(comparator_6_eq));  // open: gt, lt
  not not_1 (not_1_out, comparator_1_eq);
  not not_2 (not_2_out, comparator_4_eq);
  and and_1 (and_1_out, EX_MEM_RegWrite, not_1_out);
  and and_2 (and_2_out, MEM_WB_RegWrite, not_2_out);
  and and_3 (ForwardA[1], and_1_out, comparator_2_eq);
  and and_4 (out_8[1], and_1_out, comparator_3_eq);
  not not_3 (not_3_out, out_8[1]);
  not not_4 (not_4_out, ForwardA[1]);
  and and_5 (out_8[0], and_2_out, not_3_out, comparator_6_eq);
  and and_6 (ForwardA[0], and_2_out, not_4_out, comparator_5_eq);
endmodule

module LoadHazardUnit (
  input  [19:0] Instruction,
  input  ID_EX_MemRead,
  input  [3:0] IF_ID_RegisterRs,
  input  [3:0] IF_ID_RegisterRt,
  input  [3:0] ID_EX_RegisterRt,
  input  branch,
  input  EX_MEM_MemRead,
  input  [3:0] ID_EX_RegisterRs,
  input  [3:0] EX_MEM_RegisterRd,
  input  [3:0] ID_EX_RegisterRt_2,
  output [1:0] flushstall
);

  wire and_1_out, and_2_out, and_3_out, and_4_out, comparator_1_eq, comparator_2_eq, comparator_3_eq,
       comparator_4_eq, nor_1_out, nor_2_out, not_1_out, or_1_out, or_2_out;

  Comparator #(.width(4)) comparator_1 (
    .a(IF_ID_RegisterRs), .b(ID_EX_RegisterRt), .eq(comparator_1_eq));  // open: gt, lt
  Comparator #(.width(4)) comparator_2 (
    .a(IF_ID_RegisterRt), .b(ID_EX_RegisterRt), .eq(comparator_2_eq));  // open: gt, lt
  not not_1 (not_1_out, ID_EX_MemRead);
  Comparator #(.width(4)) comparator_3 (
    .a(ID_EX_RegisterRs), .b(EX_MEM_RegisterRd), .eq(comparator_3_eq));  // open: gt, lt
  Comparator #(.width(4)) comparator_4 (
    .a(EX_MEM_RegisterRd), .b(ID_EX_RegisterRt_2), .eq(comparator_4_eq));  // open: gt, lt
  or or_1 (or_1_out, comparator_1_eq, comparator_2_eq);
  and and_1 (and_1_out, ID_EX_MemRead, or_1_out);
  nor nor_1 (nor_1_out, comparator_1_eq, comparator_2_eq);
  nor nor_2 (nor_2_out, comparator_3_eq, comparator_4_eq);
  and and_2 (and_2_out, and_1_out, branch);
  and and_3 (and_3_out, nor_1_out, not_1_out, branch, EX_MEM_MemRead, nor_2_out);
  or or_2 (or_2_out, comparator_1_eq, comparator_2_eq);
  or or_3 (flushstall[1], and_3_out, and_2_out, and_1_out, and_4_out);
  and and_4 (and_4_out, or_2_out, not_1_out, branch);

  assign flushstall[0] = flushstall[1];

  // Notes on the sheet:
  //   01
  //   11
  //   01
  //   01
endmodule
