// Logisim project MIPS.circ as structural Verilog: 4 circuits, main circuit main
module main (
  input  CLR,
  output [7:0] PC_2__relative_to_ID_instruction,
  output [7:0] PC_1_offset__relative_to_ID_instruction,
  output [7:0] Next_PC,
  output [2:0] ALUControl,
  output [7:0] zero,
  output [7:0] t0,
  output [7:0] t1,
  output [7:0] t2,
  output [7:0] t3,
  output [7:0] t4,
  output [7:0] sp
);

  wire and_1_out, and_2_out, CLK_out, comparator_1_eq, Hazard_Unit_control__load_hazard, not_1_out,
       not_2_out, not_3_out, or_1_out, or_2_out, or_3_out;
  wire [1:0] EX__ForwardingUnit_forwarda, EX__ForwardingUnit_out_8, EX_MEM_out_8, EX_MEM_out_9,
       ID__ForwardingUnit_forwarda, ID__ForwardingUnit_out_8, ID_EX_out_13, ID_EX_out_14, MEM_WB_out_7;
  wire [3:0] EX_MEM_out_12, ID_EX_out_18, ID_EX_out_19, ID_EX_out_20, IF_ID_instruction_2,
       IF_ID_instruction_2_2, IF_ID_instruction_2_3, MEM_WB_out_10, multiplexer_8_out;
  wire [5:3] ID_EX_out_15;
  wire [7:0] alu_8_by_art_1_p4, bit_extender_1_out, EX_MEM_out_10, EX_MEM_out_11, ID_EX_out_16, ID_EX_out_17,
       ID_EX_out_21, ID_EX_out_22, IF_ID_instruction_2_4, IF_ID_pc_2, main_1_read_data_1, main_1_read_data_2,
       MEM_WB_out_8, MEM_WB_out_9, multiplexer_2_out, multiplexer_3_out, multiplexer_6_out,
       multiplexer_7_out, multiplexer_9_out, multiplexer_10_out, multiplexer_11_out, multiplexer_12_out,
       multiplexer_13_out, PC_q, ram_1_data, subtractor_1_out;
  wire [12:0] multiplexer_5_out, rom_2_data;
  wire [19:0] multiplexer_4_out, rom_1_data;

  Clock CLK (.out(CLK_out));
  Multiplexer #(.width(8), .enable("false")) multiplexer_1 (
    .in0(multiplexer_2_out), .in1({IF_ID_instruction_2_2, IF_ID_instruction_2}), .out(Next_PC),
    .sel(multiplexer_5_out[12]));
  Register PC (.D(Next_PC), .en(1'b1), .Q(PC_q), .clk(CLK_out), .clr(CLR));
  Subtractor subtractor_1 (.a(PC_q), .b(8'h2), .out(subtractor_1_out));  // open: bin, bout
  Multiplexer #(.width(8), .enable("false")) multiplexer_2 (
    .in0(PC_2__relative_to_ID_instruction), .in1(PC_1_offset__relative_to_ID_instruction),
    .out(multiplexer_2_out), .sel(or_3_out));
  Multiplexer #(.width(8), .enable("false")) multiplexer_3 (
    .in0(PC_q), .in1(subtractor_1_out), .out(multiplexer_3_out), .sel(Hazard_Unit_control__load_hazard));
  Adder adder_1 (.a(8'h1), .b(multiplexer_3_out), .out(PC_2__relative_to_ID_instruction));  // open: cin, cout
  ROM #(.dataWidth(20)) rom_1 (.addr(multiplexer_3_out), .data(rom_1_data));  // open: sel
  or or_1 (or_1_out, multiplexer_5_out[12], or_3_out, Hazard_Unit_control__load_hazard);
  Multiplexer #(.width(20), .enable("false")) multiplexer_4 (
    .in0(rom_1_data), .in1(20'h50000), .out(multiplexer_4_out), .sel(or_1_out));
  IF_ID IF_ID (
    .PC(PC_2__relative_to_ID_instruction), .Instruction(multiplexer_4_out), .CLK(CLK_out), .CLR(CLR),
    .PCEnable(1'b1), .PC_2(IF_ID_pc_2),
    .Instruction_2({IF_ID_instruction_2_3, IF_ID_instruction_2_2, IF_ID_instruction_2, IF_ID_instruction_2_4}));
  Adder adder_2 (
    .a(IF_ID_pc_2), .b(IF_ID_instruction_2_4), .out(PC_1_offset__relative_to_ID_instruction));  // open: cin, cout
  assign bit_extender_1_out = {{4{1'b0}}, IF_ID_instruction_2_4[3:0]};  // Bit_Extender bit_extender_1
  or or_2 (or_2_out, rom_2_data[5], rom_2_data[4]);
  ROM #(.addrWidth(4), .dataWidth(13)) rom_2 (.addr(IF_ID_instruction_2_3), .data(rom_2_data));  // open: sel
  LoadHazardUnit Hazard_Unit (
    .ID_EX_MemRead(ID_EX_out_14[1]), .IF_ID_RegisterRs(IF_ID_instruction_2_2),
    .ID_EX_RegisterRt(multiplexer_8_out), .IF_ID_RegisterRt(IF_ID_instruction_2),
    .EX_MEM_MemRead(EX_MEM_out_9[1]), .ID_EX_RegisterRs(ID_EX_out_18), .EX_MEM_RegisterRd(EX_MEM_out_12),
    .ID_EX_RegisterRt_2(ID_EX_out_19), .branch(or_2_out),
    .Control__Load_Hazard(Hazard_Unit_control__load_hazard));
  not not_1 (not_1_out, CLK_out);
  or or_3 (or_3_out, and_1_out, and_2_out);
  and and_1 (and_1_out, multiplexer_5_out[5], comparator_1_eq);
  not not_2 (not_2_out, comparator_1_eq);
  and and_2 (and_2_out, not_2_out, multiplexer_5_out[4]);
  Multiplexer #(.width(13), .enable("false")) multiplexer_5 (
    .in0(rom_2_data), .in1({13{1'b0}}), .out(multiplexer_5_out), .sel(Hazard_Unit_control__load_hazard));
  Register_main main_1 (
    .Read_Register_1(IF_ID_instruction_2_2), .Read_Register_2(IF_ID_instruction_2),
    .Write_Register(MEM_WB_out_10), .in_4(multiplexer_13_out), .Write_Signal(MEM_WB_out_7[1]),
    .CLK(not_1_out), .Clear(CLR), .zero(zero), .t0(t0), .t1(t1), .t2(t2), .t3(t3), .t4(t4), .sp(sp),
    .Read_Data_1(main_1_read_data_1), .Read_Data_2(main_1_read_data_2));
  Multiplexer #(.select(2), .width(8), .enable("false")) multiplexer_6 (
    .in0(main_1_read_data_1), .in1(multiplexer_13_out), .in2(EX_MEM_out_10), .out(multiplexer_6_out),
    .sel(ID__ForwardingUnit_forwarda));  // open: in3
  Multiplexer #(.select(2), .width(8), .enable("false")) multiplexer_7 (
    .in0(main_1_read_data_2), .in1(multiplexer_13_out), .in2(EX_MEM_out_10), .out(multiplexer_7_out),
    .sel(ID__ForwardingUnit_out_8));  // open: in3
  ForwardingUnit ID__ForwardingUnit (
    .EX_MEM_RegWrite(EX_MEM_out_8[1]), .EX_MEM_RegisterRd(EX_MEM_out_12),
    .ID_EX_RegisterRs(IF_ID_instruction_2_2), .ID_EX_RegisterRt(IF_ID_instruction_2),
    .MEM_WB_RegWrite(MEM_WB_out_7[0]), .MEM_WB_RegisterRd(MEM_WB_out_10),
    .ForwardA(ID__ForwardingUnit_forwarda), .out_8(ID__ForwardingUnit_out_8));
  Comparator comparator_1 (.a(multiplexer_6_out), .b(multiplexer_7_out), .eq(comparator_1_eq));  // open: gt, lt
  ID_EX ID_EX (
    .WB({multiplexer_5_out[9], multiplexer_5_out[6]}), .MEM(multiplexer_5_out[8:7]),
    .EX({multiplexer_5_out[11:10], multiplexer_5_out[3:0]}), .rs_data(main_1_read_data_1),
    .rt_data(main_1_read_data_2), .rs_address(IF_ID_instruction_2_2), .rt_address(IF_ID_instruction_2),
    .rd_address(IF_ID_instruction_2_4[7:4]), .shift_amount(bit_extender_1_out),
    .immediate_addr(IF_ID_instruction_2_4), .CLR(CLR), .CLK(CLK_out), .out_13(ID_EX_out_13),
    .out_14(ID_EX_out_14), .out_15({ID_EX_out_15, ALUControl}), .out_16(ID_EX_out_16), .out_17(ID_EX_out_17),
    .out_18(ID_EX_out_18), .out_19(ID_EX_out_19), .out_20(ID_EX_out_20), .out_21(ID_EX_out_21),
    .out_22(ID_EX_out_22));
  Multiplexer #(.width(4), .enable("false")) multiplexer_8 (
    .in0(ID_EX_out_19), .in1(ID_EX_out_20), .out(multiplexer_8_out), .sel(ID_EX_out_15[4]));
  Multiplexer #(.select(2), .width(8), .enable("false")) multiplexer_9 (
    .in0(ID_EX_out_16), .in1(multiplexer_13_out), .in2(EX_MEM_out_10), .out(multiplexer_9_out),
    .sel(EX__ForwardingUnit_forwarda));  // open: in3
  Multiplexer #(.select(2), .width(8), .enable("false")) multiplexer_10 (
    .in0(ID_EX_out_17), .in1(multiplexer_13_out), .in2(EX_MEM_out_10), .out(multiplexer_10_out),
    .sel(EX__ForwardingUnit_out_8));  // open: in3
  ForwardingUnit EX__ForwardingUnit (
    .EX_MEM_RegWrite(EX_MEM_out_8[1]), .EX_MEM_RegisterRd(EX_MEM_out_12), .ID_EX_RegisterRs(ID_EX_out_18),
    .ID_EX_RegisterRt(ID_EX_out_19), .MEM_WB_RegWrite(MEM_WB_out_7[1]), .MEM_WB_RegisterRd(MEM_WB_out_10),
    .ForwardA(EX__ForwardingUnit_forwarda), .out_8(EX__ForwardingUnit_out_8));
  Multiplexer #(.width(8), .enable("false")) multiplexer_11 (
    .in0(multiplexer_9_out), .in1(ID_EX_out_21), .out(multiplexer_11_out), .sel(ID_EX_out_15[5]));
  Multiplexer #(.width(8), .enable("false")) multiplexer_12 (
    .in0(multiplexer_10_out), .in1(ID_EX_out_22), .out(multiplexer_12_out), .sel(ID_EX_out_15[3]));
  // ALU_8_by_ART alu_8_by_art_1: pin names not known; wires that end beside it: multiplexer_11_out, multiplexer_12_out, ALUControl, alu_8_by_art_1_p4
  EX_MEM EX_MEM (
    .WB(ID_EX_out_13), .MEM(ID_EX_out_14), .ALUoutput(alu_8_by_art_1_p4), .WriteData(multiplexer_10_out),
    .rd_address(multiplexer_8_out), .CLR(CLR), .CLK(CLK_out), .out_8(EX_MEM_out_8), .out_9(EX_MEM_out_9),
    .out_10(EX_MEM_out_10), .out_11(EX_MEM_out_11), .out_12(EX_MEM_out_12));
  not not_3 (not_3_out, CLK_out);
  RAM #(.bus("separate")) ram_1 (
    .addr(EX_MEM_out_10), .din(EX_MEM_out_11), .data(ram_1_data), .str(EX_MEM_out_9[0]), .clk(not_3_out),
    .ld(EX_MEM_out_9[1]), .clr(CLR));  // open: sel
  MEM_WB MEM_WB (
    .WB(EX_MEM_out_8), .DM_read_data(ram_1_data), .ALUoutput(EX_MEM_out_10), .rd_address(EX_MEM_out_12),
    .CLR(CLR), .CLK(CLK_out), .out_7(MEM_WB_out_7), .out_8(MEM_WB_out_8), .out_9(MEM_WB_out_9),
    .out_10(MEM_WB_out_10));
  Multiplexer #(.width(8), .enable("false")) multiplexer_13 (
    .in0(MEM_WB_out_9), .in1(MEM_WB_out_8), .out(multiplexer_13_out), .sel(MEM_WB_out_7[0]));

  // Notes on the sheet:
  //   8-bit MIPS
  //   ~Prepared by~
  //   Dibbo Chowdhury (2105163)
  //   Nusrat Jahan Nidhi (2105168)
  //   Sadia Naushin (2105161)
  //   Nujhat Sadia (2105174)
  //   If hazard happens, PC is taken back to the PC of instruction in ID stage
  //   Caution: Clear once while CLK active before running any instruction
  //   avoid instruction after branch if branch is taken
  //   Instruction Memory
  //   contents of rom_1 (hex, n*v repeats v):
  //   5010a 50201 e210b 50202 e2109 50201 50301 50502 d2340 d0320 d0430 55501 215fb a0f00 50401 16400 6601
  //   80414 16100 6601 b0155 16500 6601 155a2 16500 6601 c52a2 16200 6601 52388 16300 6601 3481 f4340
  //   16400 6601 50146 50255 91230 16300 6601 334fe 16400 6601 50480 505aa 64520 16200 6601 723ff 16300
  //   6601 a3400
  //   Control Word Memory
  //   Control Word Structure:
  //   jump | shift | RegDst | RegWrite | MemRead | MemWrite | MtoR | beq | bneq | ALUSrc | ALUControl
  //   contents of rom_2 (hex, n*v repeats v):
  //   209 88 11 20b 604 208 602 20a e06 603 1000 e05 348 600 21 601
  //   Register
  //   ALU
  //   Data Memory
endmodule

module test (
  input  [3:0] in_1,
  input  [3:0] in_2,
  input  [3:0] in_3,
  input  [7:0] in_4,
  output [7:0] out_5,
  output [7:0] out_6
);

  wire clock_1_out;

  Clock clock_1 (.out(clock_1_out));
endmodule

module ForwardingUnit (
  input  EX_MEM_RegWrite,
  input  [3:0] EX_MEM_RegisterRd,
  input  [3:0] ID_EX_RegisterRs,
  input  [3:0] ID_EX_RegisterRt,
  input  MEM_WB_RegWrite,
  input  [3:0] MEM_WB_RegisterRd,
  output [1:0] ForwardA,
  output [1:0] out_8
);

  wire and_1_out, and_2_out, comparator_1_eq, comparator_2_eq, comparator_3_eq, comparator_4_eq,
       comparator_5_eq, comparator_6_eq, not_1_out, not_2_out, not_3_out, not_4_out;

  Comparator #(.width(4)) comparator_1 (.a(EX_MEM_RegisterRd), .b(4'b0000), .eq(comparator_1_eq));  // open: gt, lt
  Comparator #(.width(4)) comparator_2 (
    .a(EX_MEM_RegisterRd), .b(ID_EX_RegisterRs), .eq(comparator_2_eq));  // open: gt, lt
  Comparator #(.width(4)) comparator_3 (
    .a(EX_MEM_RegisterRd), .b(ID_EX_RegisterRt), .eq(comparator_3_eq));  // open: gt, lt
  Comparator #(.width(4)) comparator_4 (.a(MEM_WB_RegisterRd), .b(4'b0000), .eq(comparator_4_eq));  // open: gt, lt
  Comparator #(.width(4)) comparator_5 (
    .a(MEM_WB_RegisterRd), .b(ID_EX_RegisterRs), .eq(comparator_5_eq));  // open: gt, lt
  Comparator #(.width(4)) comparator_6 (
    .a(MEM_WB_RegisterRd), .b(ID_EX_RegisterRt), .eq(comparator_6_eq));  // open: gt, lt
  not not_1 (not_1_out, comparator_1_eq);
  not not_2 (not_2_out, comparator_4_eq);
  and and_1 (and_1_out, EX_MEM_RegWrite, not_1_out);
  and and_2 (and_2_out, MEM_WB_RegWrite, not_2_out);
  and and_3 (ForwardA[1], and_1_out, comparator_2_eq);
  and and_4 (out_8[1], and_1_out, comparator_3_eq);
  not not_3 (not_3_out, out_8[1]);
  not not_4 (not_4_out, ForwardA[1]);
  and and_5 (out_8[0], and_2_out, not_3_out, comparator_6_eq);
  and and_6 (ForwardA[0], and_2_out, not_4_out, comparator_5_eq);
endmodule

module LoadHazardUnit (
  input  ID_EX_MemRead,
  input  [3:0] IF_ID_RegisterRs,
  input  [3:0] ID_EX_RegisterRt,
  input  [3:0] IF_ID_RegisterRt,
  input  EX_MEM_MemRead,
  input  [3:0] ID_EX_RegisterRs,
  input  [3:0] EX_MEM_RegisterRd,
  input  [3:0] ID_EX_RegisterRt_2,
  input  branch,
  output Control__Load_Hazard
);

  wire and_1_out, and_2_out, and_3_out, and_4_out, comparator_1_eq, comparator_2_eq, comparator_3_eq,
       comparator_4_eq, nor_1_out, nor_2_out, not_1_out, or_1_out, or_2_out;

  Comparator #(.width(4)) comparator_1 (
    .a(IF_ID_RegisterRs), .b(ID_EX_RegisterRt), .eq(comparator_1_eq));  // open: gt, lt
  Comparator #(.width(4)) comparator_2 (
    .a(IF_ID_RegisterRt), .b(ID_EX_RegisterRt), .eq(comparator_2_eq));  // open: gt, lt
  Comparator #(.width(4)) comparator_3 (
    .a(ID_EX_RegisterRs), .b(EX_MEM_RegisterRd), .eq(comparator_3_eq));  // open: gt, lt
  Comparator #(.width(4)) comparator_4 (
    .a(EX_MEM_RegisterRd), .b(ID_EX_RegisterRt_2), .eq(comparator_4_eq));  // open: gt, lt
  not not_1 (not_1_out, ID_EX_MemRead);
  or or_1 (or_1_out, comparator_1_eq, comparator_2_eq);
  nor nor_1 (nor_1_out, comparator_1_eq, comparator_2_eq);
  nor nor_2 (nor_2_out, comparator_3_eq, comparator_4_eq);
  or or_2 (or_2_out, comparator_1_eq, comparator_2_eq);
  and and_1 (and_1_out, ID_EX_MemRead, or_1_out);
  and and_2 (and_2_out, nor_1_out, not_1_out, branch, EX_MEM_MemRead, nor_2_out);
  and and_3 (and_3_out, or_2_out, not_1_out, branch);
  and and_4 (and_4_out, and_1_out, branch);
  or or_3 (Control__Load_Hazard, and_1_out, and_2_out, and_3_out, and_4_out);
endmodule
