// Logisim project pipelline.circ as structural Verilog
module IF_ID (
  input  [7:0] PC,
  input  [19:0] Instruction,
  input  CLK,
  input  CLR,
  input  PCEnable,
  output [7:0] PC_2,
  output [19:0] Instruction_2
);

  Register register_1 (.D(PC), .en(PCEnable), .Q(PC_2), .clk(CLK), .clr(CLR));
  Register #(.width(20)) register_2 (.D(Instruction), .en(1'b1), .Q(Instruction_2), .clk(CLK), .clr(CLR));
endmodule

module ID_EX (
  input  [1:0] WB,
  input  [1:0] MEM,
  input  [5:0] EX,
  input  [7:0] rs_data,
  input  [7:0] rt_data,
  input  [3:0] rs_address,
  input  [3:0] rt_address,
  input  [3:0] rd_address,
  input  [7:0] shift_amount,
  input  [7:0] immediate_addr,
  input  CLR,
  input  CLK,
  output [1:0] out_13,
  output [1:0] out_14,
  output [5:0] out_15,
  output [7:0] out_16,
  output [7:0] out_17,
  output [3:0] out_18,
  output [3:0] out_19,
  output [3:0] out_20,
  output [7:0] out_21,
  output [7:0] out_22
);

  Register #(.width(2)) register_1 (.D(WB), .en(1'b1), .Q(out_13), .clk(CLK), .clr(CLR));
  Register #(.width(2)) register_2 (.D(MEM), .en(1'b1), .Q(out_14), .clk(CLK), .clr(CLR));
  Register register_3 (.D(shift_amount), .en(1'b1), .Q(out_21), .clk(CLK), .clr(CLR));
  Register register_4 (.D(immediate_addr), .en(1'b1), .Q(out_22), .clk(CLK), .clr(CLR));
  Register #(.width(6)) register_5 (.D(EX), .en(1'b1), .Q(out_15), .clk(CLK), .clr(CLR));
  Register register_6 (.D(rs_data), .en(1'b1), .Q(out_16), .clk(CLK), .clr(CLR));
  Register register_7 (.D(rt_data), .en(1'b1), .Q(out_17), .clk(CLK), .clr(CLR));
  Register #(.width(4)) register_8 (.D(rs_address), .en(1'b1), .Q(out_18), .clk(CLK), .clr(CLR));
  Register #(.width(4)) register_9 (.D(rt_address), .en(1'b1), .Q(out_19), .clk(CLK), .clr(CLR));
  Register #(.width(4)) register_10 (.D(rd_address), .en(1'b1), .Q(out_20), .clk(CLK), .clr(CLR));
endmodule

module EX_MEM (
  input  [1:0] WB,
  input  [1:0] MEM,
  input  [7:0] ALUoutput,
  input  [7:0] WriteData,
  input  [3:0] rd_address,
  input  CLR,
  input  CLK,
  output [1:0] out_8,
  output [1:0] out_9,
  output [7:0] out_10,
  output [7:0] out_11,
  output [3:0] out_12
);

  Register #(.width(2)) register_1 (.D(WB), .en(1'b1), .Q(out_8), .clk(CLK), .clr(CLR));
  Register #(.width(2)) register_2 (.D(MEM), .en(1'b1), .Q(out_9), .clk(CLK), .clr(CLR));
  Register register_3 (.D(ALUoutput), .en(1'b1), .Q(out_10), .clk(CLK), .clr(CLR));
  Register register_4 (.D(WriteData), .en(1'b1), .Q(out_11), .clk(CLK), .clr(CLR));
  Register #(.width(4)) register_5 (.D(rd_address), .en(1'b1), .Q(out_12), .clk(CLK), .clr(CLR));
endmodule

module MEM_WB (
  input  [1:0] WB,
  input  [7:0] DM_read_data,
  input  [7:0] ALUoutput,
  input  [3:0] rd_address,
  input  CLR,
  input  CLK,
  output [1:0] out_7,
  output [7:0] out_8,
  output [7:0] out_9,
  output [3:0] out_10
);

  Register #(.width(2)) register_1 (.D(WB), .en(1'b1), .Q(out_7), .clk(CLK), .clr(CLR));
  Register register_2 (.D(DM_read_data), .en(1'b1), .Q(out_8), .clk(CLK), .clr(CLR));
  Register register_3 (.D(ALUoutput), .en(1'b1), .Q(out_9), .clk(CLK), .clr(CLR));
  Register #(.width(4)) register_4 (.D(rd_address), .en(1'b1), .Q(out_10), .clk(CLK), .clr(CLR));
endmodule
