// Logisim project MIPS.circ as structural Verilog: 2 circuits, main circuit main
module main (
  input  CLR,
  output [7:0] Next_PC,
  output [7:0] PC_1,
  output [7:0] PC_1_offset,
  output [7:0] zero,
  output [2:0] ALUControl,
  output [7:0] t0,
  output [7:0] t1,
  output [7:0] t2,
  output [7:0] t3,
  output [7:0] t4,
  output [7:0] sp
);

  wire alu_8_by_art_1_p4, and_1_out, and_2_out, CLK_out, not_1_out, or_1_out;
  wire [3:0] multiplexer_2_out, rom_1_data_2;
  wire [7:0] alu_8_by_art_1_p5, bit_extender_1_out, main_1_read_data_1, main_1_read_data_2,
       multiplexer_3_out, multiplexer_4_out, multiplexer_5_out, multiplexer_6_out, PC_q, ram_1_data,
       rom_1_data, rom_1_data_3;
  wire [12:3] rom_2_data;

  Register PC (.D(Next_PC), .en(1'b1), .Q(PC_q), .clk(CLK_out), .clr(CLR));
  Clock CLK (.out(CLK_out));
  Adder adder_1 (.a(8'h1), .b(PC_q), .out(PC_1));  // open: cin, cout
  Multiplexer #(.width(8), .enable("false")) multiplexer_1 (
    .in0(multiplexer_5_out), .in1(rom_1_data), .out(Next_PC), .sel(rom_2_data[12]));
  ROM #(.dataWidth(20)) rom_1 (.addr(PC_q), .data({rom_1_data_2, rom_1_data, rom_1_data_3}));  // open: sel
  ROM #(.addrWidth(4), .dataWidth(13)) rom_2 (.addr(rom_1_data_2), .data({rom_2_data, ALUControl}));  // open: sel
  Multiplexer #(.width(4), .enable("false")) multiplexer_2 (
    .in0(rom_1_data[3:0]), .in1(rom_1_data_3[7:4]), .out(multiplexer_2_out), .sel(rom_2_data[10]));
  Register_main main_1 (
    .Read_Register_1(rom_1_data[7:4]), .Read_Register_2(rom_1_data[3:0]), .Write_Register(multiplexer_2_out),
    .in_4(multiplexer_6_out), .Write_Signal(rom_2_data[9]), .CLK(CLK_out), .Clear(CLR), .zero(zero), .t0(t0),
    .t1(t1), .t2(t2), .t3(t3), .t4(t4), .sp(sp), .Read_Data_1(main_1_read_data_1),
    .Read_Data_2(main_1_read_data_2));
  Adder adder_2 (.a(PC_1), .b(rom_1_data_3), .out(PC_1_offset));  // open: cin, cout
  assign bit_extender_1_out = {{4{1'b0}}, rom_1_data_3[3:0]};  // Bit_Extender bit_extender_1
  Multiplexer #(.width(8), .enable("false")) multiplexer_3 (
    .in0(main_1_read_data_1), .in1(bit_extender_1_out), .out(multiplexer_3_out), .sel(rom_2_data[11]));
  Multiplexer #(.width(8), .enable("false")) multiplexer_4 (
    .in0(main_1_read_data_2), .in1(rom_1_data_3), .out(multiplexer_4_out), .sel(rom_2_data[3]));
  // ALU_8_by_ART alu_8_by_art_1: pin names not known; wires that end beside it: multiplexer_3_out, multiplexer_4_out, ALUControl, alu_8_by_art_1_p4, alu_8_by_art_1_p5
  and and_1 (and_1_out, rom_2_data[4], not_1_out);
  not not_1 (not_1_out, alu_8_by_art_1_p4);
  and and_2 (and_2_out, rom_2_data[5], alu_8_by_art_1_p4);
  Multiplexer #(.width(8), .enable("false")) multiplexer_5 (
    .in0(PC_1), .in1(PC_1_offset), .out(multiplexer_5_out), .sel(or_1_out));
  or or_1 (or_1_out, and_1_out, and_2_out);
  RAM #(.bus("separate")) ram_1 (
    .addr(alu_8_by_art_1_p5), .din(main_1_read_data_2), .data(ram_1_data), .str(rom_2_data[7]),
    .clk(CLK_out), .ld(rom_2_data[8]), .clr(CLR));  // open: sel
  Multiplexer #(.width(8), .enable("false")) multiplexer_6 (
    .in0(alu_8_by_art_1_p5), .in1(ram_1_data), .out(multiplexer_6_out), .sel(rom_2_data[6]));

  // Notes on the sheet:
  //   Caution: Clear once before running any instruction
  //   Instruction Memory
  //   contents of rom_1 (hex, n*v repeats v):
  //   5011e 5020a f1210 201fe
  //   Control Word Structure:
  //   Control Word Memory
  //   contents of rom_2 (hex, n*v repeats v):
  //   209 88 11 20b 604 208 602 20a e06 603 1000 e05 348 600 21 601
  //   Register
  //   jump | shift | RegDst | RegWrite | MemRead | MemWrite | MtoR | beq | bneq | ALUSrc | ALUControl
  //   ALU
  //   Data Memory
endmodule

module test (
  input  [3:0] in_1,
  input  [3:0] in_2,
  input  [3:0] in_3,
  input  [7:0] in_4,
  output [7:0] out_5,
  output [7:0] out_6
);

  wire clock_1_out;

  Clock clock_1 (.out(clock_1_out));
endmodule
